// Logisim project CMFB-16.circ as structural Verilog: 7 circuits, main circuit FullComputer
module Computer (
  input  [6:0] Keyboard,
  input  KeyboardClock,
  output [30:0] Screen
);

  wire GPUAccess, not_1_out, Reset, Tick, WEGPU, WERAM, WR;
  wire [15:0] Data, GPUData, RAMAd, RAMData, ROMAd, RWD;
  wire [63:0] Order;

  Clock clock_1 (.out(Tick));
  Button button_1 (.out(Reset));
  CPU cpu_1 (
    .Instruction(Order), .RAMData(Data), .Clock(Tick), .Reset(Reset), .WriteRAM(WR), .RAMAddress(RAMAd),
    .ROMAddress(ROMAd), .RAMWData(RWD));
  ROM #(.addrWidth(16), .dataWidth(64)) rom_1 (.addr(ROMAd), .data(Order));
  RAM #(.addrWidth(16), .dataWidth(16)) ram_1 (
    .addr(RAMAd), .we(WERAM), .oe(1'b1), .clk(Tick), .din(RWD), .dout(RAMData));
  Comparator #(.mode("unsigned"), .width(16)) comparator_1 (.a(RAMAd), .b(16'hfff7), .gt(GPUAccess));  // open: eq, lt
  and and_1 (WERAM, WR, not_1_out);
  not not_1 (not_1_out, GPUAccess);
  and and_2 (WEGPU, WR, GPUAccess);
  Multiplexer #(.width(16)) multiplexer_1 (.in0(RAMData), .in1(GPUData), .out(Data), .sel(GPUAccess));
  Button button_2 (.out(Screen[30]));
  GPU gpu_1 (
    .Clock(Tick), .CPUInput(RWD), .GPUWE(WEGPU), .CPUAddress(RAMAd[2:0]), .Keyboard(Keyboard),
    .KeyboardClock(KeyboardClock), .WE(Screen[29]), .GPUData(GPUData), .RGB(Screen[15:0]), .X(Screen[27:22]),
    .Y(Screen[21:16]));

  assign Screen[28] = 1'b1;

  // Other names for the same wires on the sheet: RGB[15:0] = Screen[15:0]; Y[5:0] = Screen[21:16];
  //   X[5:0] = Screen[27:22]; WEScreen = Screen[29]

  // Notes on the sheet:
  //   contents of rom_1 (hex, n*v repeats v):
  //   a000000f800 a000001000a a000002000a a0000030036 a0000040036 a00000dfffd 200c0dd0000 44000d00000
  //   40800000005 a00000dfff8 a1d00000 a00000dfff9 a2d00000 a00000dfffa a3d00000 a00000dfffb a4d00000
  //   a00000dfffc a0d00000 a00000dfffd a00000e0001 aed00000 a0000010036 a000002000a a000003000a
  //   a0000040036 a00000dfffd 200c0dd0000 44000d00000 4080000001a a00000dfff8 a1d00000 a00000dfff9
  //   a2d00000 a00000dfffa a3d00000 a00000dfffb a4d00000 a00000dfffc a0d00000 a00000dfffd a00000e0001
  //   aed00000 4100000002b
endmodule

module CPU (
  input  [63:0] Instruction,
  input  [15:0] RAMData,
  input  Clock,
  input  Reset,
  output WriteRAM,
  output [15:0] RAMAddress,
  output [15:0] ROMAddress,
  output [15:0] RAMWData
);

  wire ALUSrc, C, GT, JE, MV, N, Part, ResultSrc, RRAM, URAM, V, WE, Z;
  wire [3:0] AluOp, RAddrA, RAddrB, WAddr;
  wire [15:0] adaptedalu_1_highoutput, adaptedalu_1_lowoutput, InmediateData, multiplexer_2_out,
       multiplexer_3_out, registers_1_boutput, WData;

  decode decode_1 (
    .LT(N), .Z(Z), .GT(GT), .Order(Instruction), .WriteRAM(WriteRAM), .ReadRAM(RRAM), .UseRAM(URAM),
    .Part(Part), .JE(JE), .AluOp(AluOp), .InmediateData(InmediateData), .WE(WE), .WAddr(WAddr),
    .RAddrA(RAddrA), .ALUSrc(ALUSrc), .RAddrB(RAddrB), .ResultSrc(ResultSrc));
  programCounter programcounter_1 (
    .NumberInput(RAMWData), .DirectNumber(JE), .RunCycle(Clock), .Reset(Reset), .Counter(ROMAddress));
  registers registers_1 (
    .Clock(Clock), .WData(WData), .Reset(Reset), .Part(Part), .WE(WE), .WAddr(WAddr), .RAddrA(RAddrA),
    .RAddrB(RAddrB), .ALUOp(AluOp), .AOutput(RAMAddress), .BOutput(registers_1_boutput));
  Multiplexer #(.width(16)) multiplexer_1 (
    .in0(registers_1_boutput), .in1(InmediateData), .out(RAMWData), .sel(ALUSrc));
  adaptedALU adaptedalu_1 (
    .Cin(C), .AInput(RAMAddress), .BInput(RAMWData), .ControlInput(AluOp), .Clock(Clock),
    .FlagsRegister({Z, MV, N, V, C, GT}), .LowOutput(adaptedalu_1_lowoutput),
    .HighOutput(adaptedalu_1_highoutput));
  Multiplexer #(.width(16)) multiplexer_2 (
    .in0(adaptedalu_1_lowoutput), .in1(adaptedalu_1_highoutput), .out(multiplexer_2_out), .sel(Part));
  Multiplexer #(.width(16)) multiplexer_3 (
    .in0(multiplexer_2_out), .in1(InmediateData), .out(multiplexer_3_out), .sel(ResultSrc));
  Multiplexer #(.width(16)) multiplexer_4 (.in0(multiplexer_3_out), .in1(RAMData), .out(WData), .sel(RRAM));

  // Other names for the same wires on the sheet: Counter[15:0] = ROMAddress; JumpDir[15:0] = RAMWData;
  //   Order[63:0] = Instruction; Tick = Clock
endmodule

module programCounter (
  input  [15:0] NumberInput,
  input  DirectNumber,
  input  RunCycle,
  input  Reset,
  output [15:0] Counter
);

  wire not_1_out;
  wire [1:0] minihalfadder_1_dataoutput, minihalfadder_2_dataoutput, minihalfadder_3_dataoutput,
       minihalfadder_4_dataoutput, minihalfadder_5_dataoutput, minihalfadder_6_dataoutput,
       minihalfadder_7_dataoutput, minihalfadder_8_dataoutput, minihalfadder_9_dataoutput,
       minihalfadder_10_dataoutput, minihalfadder_11_dataoutput, minihalfadder_12_dataoutput,
       minihalfadder_13_dataoutput, minihalfadder_14_dataoutput, minihalfadder_15_dataoutput,
       minihalfadder_16_dataoutput;
  wire [15:0] multiplexer_1_out, register_1_q, reverse_1_dataoutput;

  minihalfadder minihalfadder_1 (
    .AInput(register_1_q[0]), .BInput(minihalfadder_2_dataoutput[0]), .DataOutput(minihalfadder_1_dataoutput));
  minihalfadder minihalfadder_2 (
    .AInput(register_1_q[1]), .BInput(minihalfadder_3_dataoutput[0]), .DataOutput(minihalfadder_2_dataoutput));
  minihalfadder minihalfadder_3 (
    .AInput(register_1_q[2]), .BInput(minihalfadder_4_dataoutput[0]), .DataOutput(minihalfadder_3_dataoutput));
  minihalfadder minihalfadder_4 (
    .AInput(register_1_q[3]), .BInput(minihalfadder_5_dataoutput[0]), .DataOutput(minihalfadder_4_dataoutput));
  minihalfadder minihalfadder_5 (
    .AInput(register_1_q[4]), .BInput(minihalfadder_6_dataoutput[0]), .DataOutput(minihalfadder_5_dataoutput));
  minihalfadder minihalfadder_6 (
    .AInput(register_1_q[5]), .BInput(minihalfadder_7_dataoutput[0]), .DataOutput(minihalfadder_6_dataoutput));
  minihalfadder minihalfadder_7 (
    .AInput(register_1_q[6]), .BInput(minihalfadder_8_dataoutput[0]), .DataOutput(minihalfadder_7_dataoutput));
  minihalfadder minihalfadder_8 (
    .AInput(register_1_q[7]), .BInput(minihalfadder_9_dataoutput[0]), .DataOutput(minihalfadder_8_dataoutput));
  minihalfadder minihalfadder_9 (
    .AInput(register_1_q[8]), .BInput(minihalfadder_10_dataoutput[0]), .DataOutput(minihalfadder_9_dataoutput));
  minihalfadder minihalfadder_10 (
    .AInput(register_1_q[9]), .BInput(minihalfadder_11_dataoutput[0]),
    .DataOutput(minihalfadder_10_dataoutput));
  minihalfadder minihalfadder_11 (
    .AInput(register_1_q[10]), .BInput(minihalfadder_12_dataoutput[0]),
    .DataOutput(minihalfadder_11_dataoutput));
  minihalfadder minihalfadder_12 (
    .AInput(register_1_q[11]), .BInput(minihalfadder_13_dataoutput[0]),
    .DataOutput(minihalfadder_12_dataoutput));
  minihalfadder minihalfadder_13 (
    .AInput(register_1_q[12]), .BInput(minihalfadder_14_dataoutput[0]),
    .DataOutput(minihalfadder_13_dataoutput));
  minihalfadder minihalfadder_14 (
    .AInput(register_1_q[13]), .BInput(minihalfadder_15_dataoutput[0]),
    .DataOutput(minihalfadder_14_dataoutput));
  minihalfadder minihalfadder_15 (
    .AInput(register_1_q[14]), .BInput(minihalfadder_16_dataoutput[0]),
    .DataOutput(minihalfadder_15_dataoutput));
  minihalfadder minihalfadder_16 (.AInput(register_1_q[15]), .BInput(1'b1), .DataOutput(minihalfadder_16_dataoutput));
  not not_1 (not_1_out, DirectNumber);
  Register #(.width(16)) register_1 (.D(multiplexer_1_out), .en(1'b1), .clk(RunCycle), .Q(register_1_q), .clr(Reset));
  Multiplexer #(.width(16)) multiplexer_1 (
    .in0(reverse_1_dataoutput),
    .in1({minihalfadder_16_dataoutput[1], minihalfadder_15_dataoutput[1], minihalfadder_14_dataoutput[1], minihalfadder_13_dataoutput[1], minihalfadder_12_dataoutput[1], minihalfadder_11_dataoutput[1], minihalfadder_10_dataoutput[1], minihalfadder_9_dataoutput[1], minihalfadder_8_dataoutput[1], minihalfadder_7_dataoutput[1], minihalfadder_6_dataoutput[1], minihalfadder_5_dataoutput[1], minihalfadder_4_dataoutput[1], minihalfadder_3_dataoutput[1], minihalfadder_2_dataoutput[1], minihalfadder_1_dataoutput[1]}),
    .out(multiplexer_1_out), .sel(not_1_out));
  reverse reverse_1 (.DataInput(NumberInput), .DataOutput(reverse_1_dataoutput));
  reverse reverse_2 (.DataInput(register_1_q), .DataOutput(Counter));
endmodule

module registers (
  input  Clock,
  input  [15:0] WData,
  input  Reset,
  input  Part,
  input  WE,
  input  [3:0] WAddr,
  input  [3:0] RAddrA,
  input  [3:0] RAddrB,
  input  [3:0] ALUOp,
  output [15:0] AOutput,
  output [15:0] BOutput
);

  wire decoder_1_out0, decoder_1_out1, decoder_1_out2, decoder_1_out3, decoder_1_out4, decoder_1_out5,
       decoder_1_out6, decoder_1_out7, decoder_1_out8, decoder_1_out9, decoder_1_out10, decoder_1_out11,
       decoder_1_out12, decoder_1_out13, decoder_1_out14, decoder_1_out15, decoder_2_out10, not_1_out;
  wire [15:0] MulLatch, multiplexer_1_out, R0, R1, R2, R3, R4, R5, R6, R7, R8, R9, R10, R11, R12, R13, R14,
       R15;

  Decoder #(.select(4)) decoder_1 (
    .out0(decoder_1_out0), .out1(decoder_1_out1), .out2(decoder_1_out2), .out3(decoder_1_out3),
    .out4(decoder_1_out4), .out5(decoder_1_out5), .out6(decoder_1_out6), .out7(decoder_1_out7),
    .out8(decoder_1_out8), .out9(decoder_1_out9), .out10(decoder_1_out10), .out11(decoder_1_out11),
    .out12(decoder_1_out12), .out13(decoder_1_out13), .out14(decoder_1_out14), .out15(decoder_1_out15),
    .sel(WAddr), .en(WE));
  not not_1 (not_1_out, Part);
  Decoder #(.select(4)) decoder_2 (
    .out10(decoder_2_out10), .sel(ALUOp), .en(not_1_out));  // open: out0, out1, out2, out3, out4, out5, out6, out7, out8, out9, out11, out12, out13, out14, out15
  Register #(.width(16)) register_1 (.D(WData), .en(decoder_1_out0), .clk(Clock), .Q(R0), .clr(Reset));
  Register #(.width(16)) register_2 (.D(WData), .en(decoder_1_out1), .clk(Clock), .Q(R1), .clr(Reset));
  Register #(.width(16)) register_3 (.D(WData), .en(decoder_1_out2), .clk(Clock), .Q(R2), .clr(Reset));
  Register #(.width(16)) register_4 (.D(WData), .en(decoder_1_out3), .clk(Clock), .Q(R3), .clr(Reset));
  Register #(.width(16)) register_5 (.D(WData), .en(decoder_1_out4), .clk(Clock), .Q(R4), .clr(Reset));
  Register #(.width(16)) register_6 (.D(WData), .en(decoder_1_out5), .clk(Clock), .Q(R5), .clr(Reset));
  Register #(.width(16)) register_7 (.D(WData), .en(decoder_1_out6), .clk(Clock), .Q(R6), .clr(Reset));
  Register #(.width(16)) register_8 (.D(WData), .en(decoder_1_out7), .clk(Clock), .Q(R7), .clr(Reset));
  Register #(.width(16)) register_9 (.D(WData), .en(decoder_1_out8), .clk(Clock), .Q(R8), .clr(Reset));
  Register #(.width(16)) register_10 (.D(WData), .en(decoder_1_out9), .clk(Clock), .Q(R9), .clr(Reset));
  Register #(.width(16)) register_11 (.D(WData), .en(decoder_1_out10), .clk(Clock), .Q(R10), .clr(Reset));
  Register #(.width(16)) register_12 (.D(WData), .en(decoder_1_out11), .clk(Clock), .Q(R11), .clr(Reset));
  Register #(.width(16)) register_13 (.D(WData), .en(decoder_1_out12), .clk(Clock), .Q(R12), .clr(Reset));
  Register #(.width(16)) register_14 (.D(WData), .en(decoder_1_out13), .clk(Clock), .Q(R13), .clr(Reset));
  Register #(.width(16)) register_15 (.D(WData), .en(decoder_1_out14), .clk(Clock), .Q(R14), .clr(Reset));
  Register #(.width(16)) register_16 (.D(WData), .en(decoder_1_out15), .clk(Clock), .Q(R15), .clr(Reset));
  Register #(.width(16)) register_17 (.D(AOutput), .en(decoder_2_out10), .clk(Clock), .Q(MulLatch), .clr(Reset));
  Multiplexer #(.select(4), .width(16)) multiplexer_1 (
    .in0(R0), .in1(R1), .in2(R2), .in3(R3), .in4(R4), .in5(R5), .in6(R6), .in7(R7), .in8(R8), .in9(R9),
    .in10(R10), .in11(R11), .in12(R12), .in13(R13), .in14(R14), .in15(R15), .out(multiplexer_1_out),
    .sel(RAddrA));
  Multiplexer #(.select(4), .width(16)) multiplexer_2 (
    .in0(R0), .in1(R1), .in2(R2), .in3(R3), .in4(R4), .in5(R5), .in6(R6), .in7(R7), .in8(R8), .in9(R9),
    .in10(R10), .in11(R11), .in12(R12), .in13(R13), .in14(R14), .in15(R15), .out(BOutput), .sel(RAddrB));
  Multiplexer #(.width(16)) multiplexer_3 (.in0(multiplexer_1_out), .in1(MulLatch), .out(AOutput), .sel(Part));

  // Other names for the same wires on the sheet: LatchData[15:0] = AOutput
endmodule

module adaptedALU (
  input  Cin,
  input  [15:0] AInput,
  input  [15:0] BInput,
  input  [3:0] ControlInput,
  input  Clock,
  output [5:0] FlagsRegister,
  output [15:0] LowOutput,
  output [15:0] HighOutput
);

  wire button_1_out;
  wire [5:0] alu_1_flagsbus;
  wire [15:0] alu_1_highoutput, alu_1_lowoutput, reverse_1_dataoutput, reverse_2_dataoutput;

  reverse reverse_1 (.DataInput(AInput), .DataOutput(reverse_1_dataoutput));
  reverse reverse_2 (.DataInput(BInput), .DataOutput(reverse_2_dataoutput));
  ALU alu_1 (
    .AInput(reverse_1_dataoutput), .BInput(reverse_2_dataoutput), .Cin(Cin),
    .ControlInput({ControlInput[0], ControlInput[1], ControlInput[2], ControlInput[3]}),
    .HighOutput(alu_1_highoutput), .LowOutput(alu_1_lowoutput), .FlagsBus(alu_1_flagsbus));
  reverse reverse_3 (.DataInput(alu_1_highoutput), .DataOutput(HighOutput));
  reverse reverse_4 (.DataInput(alu_1_lowoutput), .DataOutput(LowOutput));
  Register #(.width(6)) register_1 (.D(alu_1_flagsbus), .en(1'b1), .clk(Clock), .Q(FlagsRegister), .clr(button_1_out));
  Button button_1 (.out(button_1_out));
endmodule

module decode (
  input  LT,
  input  Z,
  input  GT,
  input  [63:0] Order,
  output WriteRAM,
  output ReadRAM,
  output UseRAM,
  output Part,
  output JE,
  output [3:0] AluOp,
  output [15:0] InmediateData,
  output WE,
  output [3:0] WAddr,
  output [3:0] RAddrA,
  output ALUSrc,
  output [3:0] RAddrB,
  output ResultSrc
);

  wire JE1, JE2, JE3;

  LED led_1 (.in(Order[20]));
  LED led_2 (.in(Order[24]));
  LED led_3 (.in(Order[21]));
  LED led_4 (.in(Order[25]));
  LED led_5 (.in(Order[22]));
  LED led_6 (.in(Order[26]));
  LED led_7 (.in(Order[23]));
  LED led_8 (.in(Order[27]));
  LED led_9 (.in(Order[16]));
  LED led_10 (.in(Order[17]));
  LED led_11 (.in(Order[18]));
  LED led_12 (.in(Order[19]));
  LED led_13 (.in(Order[0]));
  LED led_14 (.in(Order[1]));
  LED led_15 (.in(Order[2]));
  LED led_16 (.in(Order[3]));
  LED led_17 (.in(Order[4]));
  LED led_18 (.in(Order[5]));
  LED led_19 (.in(Order[6]));
  LED led_20 (.in(Order[7]));
  LED led_21 (.in(Order[8]));
  LED led_22 (.in(Order[9]));
  LED led_23 (.in(Order[10]));
  LED led_24 (.in(Order[11]));
  LED led_25 (.in(Order[12]));
  LED led_26 (.in(Order[13]));
  LED led_27 (.in(Order[14]));
  LED led_28 (.in(Order[15]));
  and and_1 (JE3, LT, Order[33]);
  and and_2 (JE2, Z, Order[34]);
  or or_1 (JE, JE3, JE2, JE1, Order[36]);
  and and_3 (JE1, GT, Order[35]);

  assign AluOp = Order[40:37];
  assign ALUSrc = Order[42];
  assign InmediateData = Order[15:0];
  assign Part = Order[32];
  assign RAddrA = Order[23:20];
  assign RAddrB = Order[27:24];
  assign ReadRAM = Order[30];
  assign ResultSrc = Order[43];
  assign UseRAM = Order[31];
  assign WAddr = Order[19:16];
  assign WE = Order[41];
  assign WriteRAM = Order[29];

  // Other names for the same wires on the sheet: JE0 = Order[36]
endmodule

module FullComputer (
);

  wire keyboard_1_avail;
  wire [5:0] rgb_video_1_p4, rgb_video_1_p5;
  wire [6:0] keyboard_1_data;
  wire [15:0] rgb_video_1_p6;
  wire [30:28] rgb_video_1_p3;

  Keyboard keyboard_1 (.clr(keyboard_1_avail), .avail(keyboard_1_avail), .data(keyboard_1_data));  // open: clk, re
  // RGB_Video #(.cursor("No Cursor"), .height(64), .scale(8), .width(64)) rgb_video_1: pin names not known; wires that end beside it: rgb_video_1_p3[30], rgb_video_1_p3[29], rgb_video_1_p3[28], rgb_video_1_p4, rgb_video_1_p5, rgb_video_1_p6
  Computer computer_1 (
    .Keyboard(keyboard_1_data), .KeyboardClock(keyboard_1_avail),
    .Screen({rgb_video_1_p3, rgb_video_1_p4, rgb_video_1_p5, rgb_video_1_p6}));
endmodule
