// Logisim project GMFB.circ as structural Verilog: 6 circuits, main circuit test
module GPU (
  input  Clock,
  input  [15:0] CPUInput,
  input  GPUWE,
  input  [2:0] CPUAddress,
  input  [6:0] Keyboard,
  input  KeyboardClock,
  output WE,
  output [15:0] GPUData,
  output [15:0] RGB,
  output [5:0] X,
  output [5:0] Y
);

  wire button_1_out;
  wire [15:0] RAMAddr, RAMWData, ROMAddr;
  wire [63:0] Instruction;

  Button button_1 (.out(button_1_out));
  GCPU gcpu_1 (
    .Instruction(Instruction), .RAMData({16{1'b0}}), .Clock(Clock), .CPUInput(CPUInput), .GPUWE(GPUWE),
    .CPUAddress(CPUAddress), .Keyboard(Keyboard), .Reset(button_1_out), .KeyboardClock(KeyboardClock),
    .WriteRAM(WE), .RAMAddress(RAMAddr), .GPUData(GPUData), .ROMAddress(ROMAddr), .RAMWData(RAMWData),
    .Color(RGB));
  ROM #(.addrWidth(16), .dataWidth(64)) rom_1 (.addr(ROMAddr), .data(Instruction));
  Bit_Extender #(.in_width(16), .out_width(12)) bit_extender_1 (.in(RAMAddr), .out({Y, X}));

  // Other names for the same wires on the sheet: Cl = Clock

  // Notes on the sheet:
  //   contents of rom_1 (hex, n*v repeats v):
  //   e0000090001 10009f00000 400000000e e0000090002 10009f00000 4000000007 800000005c e0000030000
  //   e0000080fff 88e300000 10008300000 400000005c 60000330001 8000000009 60000a40000 60000b50000
  //   3000ac00000 e0000090000 10009000000 2000000016 e0000060001 8000000019 e000006ffff e0000090000
  //   30000900000 3000bd10000 e0000090000 10009100000 200000001f e0000070001 8000000022 e000007ffff
  //   e0000090000 30001910000 10001000000 2000000040 20001120000 30000220000 60000080000 20005530000
  //   5*20003330000 20004330000 88e300000 e0000090000 10009800000 400000005c 20006440000 e0000090000
  //   10009200000 200000003c 20007550000 20001190000 20009220000 20000090000 30009220000 800000003e
  //   20001190000 20009220000 70000880001 8000000027 20000020000 30001220000 60000180000 20005530000
  //   5*20003330000 20004330000 88e300000 e0000090000 10009800000 400000005c 20007550000 e0000090000
  //   10009200000 2000000058 20006440000 20000090000 20009220000 20001190000 30009220000 800000005a
  //   20000090000 20009220000 70000880001 8000000043 e00000f0000
endmodule

module GCPU (
  input  [63:0] Instruction,
  input  [15:0] RAMData,
  input  Clock,
  input  [15:0] CPUInput,
  input  GPUWE,
  input  [2:0] CPUAddress,
  input  [6:0] Keyboard,
  input  Reset,
  input  KeyboardClock,
  output WriteRAM,
  output [15:0] RAMAddress,
  output [15:0] GPUData,
  output [15:0] ROMAddress,
  output [15:0] RAMWData,
  output [15:0] Color
);

  wire ActiveOp, AluOp, ALUSrc, JE, N, Reset_t, ResultSrc, RRAM, WE, Z;
  wire [3:0] RAddrA, RAddrB, WAddr;
  wire [15:0] galu_1_dataoutput, InmediateData, ioregisters_1_boutput, multiplexer_2_out, WData;

  Counter #(.max('hffff), .width(16)) counter_1 (
    .load(JE), .D(InmediateData), .Q(ROMAddress), .up(1'b1), .clk(Clock), .clr(Reset_t));  // open: count, carry
  or or_1 (Reset_t, ActiveOp, Reset);
  Gdecoder gdecoder_1 (
    .LT(N), .Z(Z), .Order(Instruction), .WriteRAM(WriteRAM), .ReadRAM(RRAM), .AluOp(AluOp),
    .InmediateData(InmediateData), .WE(WE), .WAddr(WAddr), .RAddrA(RAddrA), .ALUSrc(ALUSrc), .RAddrB(RAddrB),
    .ResultSrc(ResultSrc), .JE(JE));
  IOregisters ioregisters_1 (
    .Cl(Clock), .WData(WData), .Reset(Reset_t), .WE(WE), .WAddr(WAddr), .RAddrA(RAddrA), .RAddrB(RAddrB),
    .CPUInput(CPUInput), .GPUWE(GPUWE), .CPUAddress(CPUAddress), .Keyboard(Keyboard),
    .KeyboardClock(KeyboardClock), .AOutput(RAMAddress), .BOutput(ioregisters_1_boutput), .GPUData(GPUData),
    .ActiveOperation(ActiveOp), .Color(Color));
  Multiplexer #(.width(16)) multiplexer_1 (
    .in0(ioregisters_1_boutput), .in1(InmediateData), .out(RAMWData), .sel(ALUSrc));
  GALU galu_1 (
    .ControlInput(AluOp), .AInput(RAMAddress), .BInput(RAMWData), .Clock(Clock),
    .DataOutput(galu_1_dataoutput), .FlagsRegister({N, Z}));
  Multiplexer #(.width(16)) multiplexer_2 (
    .in0(galu_1_dataoutput), .in1(InmediateData), .out(multiplexer_2_out), .sel(ResultSrc));
  Multiplexer #(.width(16)) multiplexer_3 (.in0(multiplexer_2_out), .in1(RAMData), .out(WData), .sel(RRAM));

  // Other names for the same wires on the sheet: Order[63:0] = Instruction; Tick = Clock
endmodule

module Gdecoder (
  input  LT,
  input  Z,
  input  [63:0] Order,
  output WriteRAM,
  output ReadRAM,
  output AluOp,
  output [15:0] InmediateData,
  output WE,
  output [3:0] WAddr,
  output [3:0] RAddrA,
  output ALUSrc,
  output [3:0] RAddrB,
  output ResultSrc,
  output JE
);

  wire JE1, JE2;

  LED led_1 (.in(Order[24]));
  LED led_2 (.in(Order[25]));
  LED led_3 (.in(Order[26]));
  LED led_4 (.in(Order[27]));
  LED led_5 (.in(Order[16]));
  LED led_6 (.in(Order[20]));
  LED led_7 (.in(Order[17]));
  LED led_8 (.in(Order[21]));
  LED led_9 (.in(Order[18]));
  LED led_10 (.in(Order[22]));
  LED led_11 (.in(Order[19]));
  LED led_12 (.in(Order[23]));
  LED led_13 (.in(Order[0]));
  LED led_14 (.in(Order[1]));
  LED led_15 (.in(Order[2]));
  LED led_16 (.in(Order[3]));
  LED led_17 (.in(Order[4]));
  LED led_18 (.in(Order[5]));
  LED led_19 (.in(Order[6]));
  LED led_20 (.in(Order[7]));
  LED led_21 (.in(Order[8]));
  LED led_22 (.in(Order[9]));
  LED led_23 (.in(Order[10]));
  LED led_24 (.in(Order[11]));
  LED led_25 (.in(Order[12]));
  LED led_26 (.in(Order[13]));
  LED led_27 (.in(Order[14]));
  LED led_28 (.in(Order[15]));
  and and_1 (JE2, LT, Order[37]);
  and and_2 (JE1, Z, Order[38]);
  or or_1 (JE, JE2, JE1, Order[39]);

  assign AluOp = Order[40];
  assign ALUSrc = Order[42];
  assign InmediateData = Order[15:0];
  assign RAddrA = Order[23:20];
  assign RAddrB = Order[27:24];
  assign ReadRAM = Order[36];
  assign ResultSrc = Order[43];
  assign WAddr = Order[19:16];
  assign WE = Order[41];
  assign WriteRAM = Order[35];

  // Other names for the same wires on the sheet: JE0 = Order[39]
endmodule

module GALU (
  input  ControlInput,
  input  [15:0] AInput,
  input  [15:0] BInput,
  input  Clock,
  output [15:0] DataOutput,
  output [1:0] FlagsRegister
);

  wire adder_1_cout, button_1_out;
  wire [1:0] comparator_1_eq;
  wire [15:0] adder_1_out, subtractor_1_out;

  Adder #(.width(16)) adder_1 (.a(AInput), .b(BInput), .out(adder_1_out), .cout(adder_1_cout));  // open: cin
  Subtractor #(.width(16)) subtractor_1 (
    .a(AInput), .b(BInput), .out(subtractor_1_out), .bin(adder_1_cout));  // open: bout
  Multiplexer #(.width(16)) multiplexer_1 (
    .in0(adder_1_out), .in1(subtractor_1_out), .out(DataOutput), .sel(ControlInput));
  Register #(.width(2)) register_1 (.D(comparator_1_eq), .en(1'b1), .clk(Clock), .Q(FlagsRegister), .clr(button_1_out));
  Comparator #(.width(16)) comparator_1 (
    .a(AInput), .b(BInput), .eq(comparator_1_eq[0]), .lt(comparator_1_eq[1]));  // open: gt
  Button button_1 (.out(button_1_out));

  // Other names for the same wires on the sheet: A[15:0] = AInput; B[15:0] = BInput
endmodule

module IOregisters (
  input  Cl,
  input  [15:0] WData,
  input  Reset,
  input  WE,
  input  [3:0] WAddr,
  input  [3:0] RAddrA,
  input  [3:0] RAddrB,
  input  [15:0] CPUInput,
  input  GPUWE,
  input  [2:0] CPUAddress,
  input  [6:0] Keyboard,
  input  KeyboardClock,
  output [15:0] AOutput,
  output [15:0] BOutput,
  output [15:0] GPUData,
  output ActiveOperation,
  output [15:0] Color
);

  wire comparator_1_gt, decoder_1_out0, decoder_1_out1, decoder_1_out2, decoder_1_out3, decoder_1_out4,
       decoder_1_out5, decoder_1_out6, decoder_1_out7, decoder_1_out8, decoder_1_out9, decoder_1_out15,
       decoder_2_out0, decoder_2_out1, decoder_2_out2, decoder_2_out3, decoder_2_out4, decoder_2_out5,
       decoder_2_out6, or_1_out, or_2_out, or_3_out;
  wire [6:0] register_17_q;
  wire [15:0] I, R0, R1, R2, R3, R4, R5, R6, R7, R8, R9, R10, R11, R12, R13, R15;

  Decoder #(.select(4)) decoder_1 (
    .out0(decoder_1_out0), .out1(decoder_1_out1), .out2(decoder_1_out2), .out3(decoder_1_out3),
    .out4(decoder_1_out4), .out5(decoder_1_out5), .out6(decoder_1_out6), .out7(decoder_1_out7),
    .out8(decoder_1_out8), .out9(decoder_1_out9), .out15(decoder_1_out15), .sel(WAddr), .en(WE));  // open: out10, out11, out12, out13, out14
  Decoder #(.select(3)) decoder_2 (
    .out0(decoder_2_out0), .out1(decoder_2_out1), .out2(decoder_2_out2), .out3(decoder_2_out3),
    .out4(decoder_2_out4), .out5(decoder_2_out5), .out6(decoder_2_out6), .sel(CPUAddress), .en(GPUWE));  // open: out7
  Register #(.width(16)) register_1 (.D(WData), .en(decoder_1_out0), .clk(Cl), .Q(R0), .clr(Reset));
  Register #(.width(16)) register_2 (.D(WData), .en(decoder_1_out1), .clk(Cl), .Q(R1), .clr(Reset));
  Register #(.width(16)) register_3 (.D(WData), .en(decoder_1_out2), .clk(Cl), .Q(R2), .clr(Reset));
  Register #(.width(16)) register_4 (.D(WData), .en(decoder_1_out3), .clk(Cl), .Q(R3), .clr(Reset));
  Register #(.width(16)) register_5 (.D(WData), .en(decoder_1_out4), .clk(Cl), .Q(R4), .clr(Reset));
  Register #(.width(16)) register_6 (.D(WData), .en(decoder_1_out5), .clk(Cl), .Q(R5), .clr(Reset));
  Register #(.width(16)) register_7 (.D(WData), .en(decoder_1_out6), .clk(Cl), .Q(R6), .clr(Reset));
  Register #(.width(16)) register_8 (.D(WData), .en(decoder_1_out7), .clk(Cl), .Q(R7), .clr(Reset));
  Register #(.width(16)) register_9 (.D(WData), .en(decoder_1_out8), .clk(Cl), .Q(R8), .clr(Reset));
  Register #(.width(16)) register_10 (.D(WData), .en(decoder_1_out9), .clk(Cl), .Q(R9), .clr(Reset));
  Register #(.width(16)) register_11 (.D(CPUInput), .en(decoder_2_out0), .clk(Cl), .Q(R10));  // open: clr
  Register #(.width(16)) register_12 (.D(CPUInput), .en(decoder_2_out1), .clk(Cl), .Q(R11));  // open: clr
  Register #(.width(16)) register_13 (.D(CPUInput), .en(decoder_2_out2), .clk(Cl), .Q(R12));  // open: clr
  Register #(.width(16)) register_14 (.D(CPUInput), .en(decoder_2_out3), .clk(Cl), .Q(R13));  // open: clr
  Register #(.width(16)) register_15 (.D(CPUInput), .en(decoder_2_out4), .clk(Cl), .Q(Color));  // open: clr
  Register #(.width(16)) register_16 (.D(CPUInput), .en(or_1_out), .clk(Cl), .Q(R15), .clr(comparator_1_gt));
  or or_1 (or_1_out, decoder_2_out5, decoder_1_out15);
  Comparator #(.mode("unsigned"), .width(16)) comparator_1 (.a(R15), .b(16'h2), .gt(comparator_1_gt));  // open: eq, lt
  Register #(.width(7)) register_17 (.D(Keyboard), .en(or_2_out), .clk(or_3_out), .Q(register_17_q));  // open: clr
  or or_2 (or_2_out, decoder_2_out6, KeyboardClock);
  or or_3 (or_3_out, decoder_2_out6, KeyboardClock);
  assign I = {{9{register_17_q[6]}}, register_17_q};  // Bit_Extender bit_extender_1
  Multiplexer #(.select(3), .width(16)) multiplexer_1 (
    .in0(R10), .in1(R11), .in2(R12), .in3(R13), .in4(Color), .in5(R15), .in6(I), .in7({16{1'b0}}),
    .out(GPUData), .sel(CPUAddress));
  nor nor_1 (ActiveOperation, R15[1], R15[0]);
  Multiplexer #(.select(4), .width(16)) multiplexer_2 (
    .in0(R0), .in1(R1), .in2(R2), .in3(R3), .in4(R4), .in5(R5), .in6(R6), .in7(R7), .in8(R8), .in9(R9),
    .in10(R10), .in11(R11), .in12(R12), .in13(R13), .in14(Color), .in15(R15), .out(AOutput), .sel(RAddrA));
  Multiplexer #(.select(4), .width(16)) multiplexer_3 (
    .in0(R0), .in1(R1), .in2(R2), .in3(R3), .in4(R4), .in5(R5), .in6(R6), .in7(R7), .in8(R8), .in9(R9),
    .in10(R10), .in11(R11), .in12(R12), .in13(R13), .in14(Color), .in15(R15), .out(BOutput), .sel(RAddrB));

  // Other names for the same wires on the sheet: CPUAddr[2:0] = CPUAddress; R14[15:0] = Color
endmodule

module test (
);

  wire button_1_out, Cl, clock_1_out, WE;
  wire [5:0] X, Y;
  wire [6:0] undriven;
  wire [15:0] RGB;

  Clock clock_1 (.out(clock_1_out));
  or or_1 (Cl, clock_1_out, button_1_out);
  Button button_1 (.out(button_1_out));
  GPU gpu_1 (
    .Clock(Cl), .CPUInput({16{1'b0}}), .GPUWE(1'b0), .CPUAddress(3'b000), .Keyboard(undriven), .WE(WE),
    .RGB(RGB), .X(X), .Y(Y));  // open: KeyboardClock, GPUData
  Button button_2 ();  // open: out
  // RGB_Video #(.height(64), .scale(8), .width(64)) rgb_video_1: pin names not known; wires that end beside it: WE, 1'b1, X, Y, RGB
endmodule
